// Logisim project ЛИК.circ as structural Verilog: 9 circuits, main circuit main
module main (
  input  START,
  input  RESET,
  output C1_C2_RG,
  output V_RG,
  output RAS_RAM_CS1_R6_A_MX,
  output \Ф2_CPU ,
  output \Ф1_CPU ,
  output A_VD3,
  output A_VD2,
  output T1,
  output T2,
  output T3,
  output T4,
  output T5,
  output T6,
  output T7,
  output T8,
  output T9,
  output T10,
  output T11,
  output T12,
  output T13,
  output T14,
  output T15,
  output T16,
  output T17,
  output T18
);

  wire and_1_out, clock_1_out, nand_1_out, nand_2_out, nand_3_out, nand_4_out, nor_1_out, nor_2_out,
       nor_3_out, nor_4_out, not_1_out, not_2_out, not_3_out, \к555ид4_1_na0__7 , \к555ид4_1_na1__6 ,
       \к555ид4_1_na2__5 , \к555ид4_1_na3__4 , \к555ид4_1_nb0__9 , \к555ид4_1_nb2__11 , \к555ие5_3__4__8 ,
       \к555ие5_3__8__11 , \к555ие7_1_p___12 , \к555ие7_1_p___13 , \к555ие7_2__1__3 , \к555ие7_2__4__6 ,
       \к555ие7_2_p___12 , \к555ие7_2_p___13 ;

  Clock clock_1 (.out(clock_1_out));
  \К555ИЕ7  \u_к555ие7_1  (
    .D1__15(1'b1), .minus_1__4(1'b1), .plus_1__5(\к555ие7_2_p___12 ), .D2__1(1'b1), .D4__10(1'b1),
    .D8__9(1'b1), .R__14(RESET), .V__11(1'b1), .P___13(\к555ие7_1_p___13 ), .P___12(\к555ие7_1_p___12 ),
    ._1__3(T2), ._2__2(T3), ._4__6(T4), ._8__7(T5));
  \К555ИЕ5  \u_к555ие5_1  (
    .C2__14(T5), .C1__1(A_VD3), .R0__2(RESET), .R0__3(RESET), ._1__12(T6), ._2__9(T7), ._4__8(T8), ._8__11(T9));
  \К555ИЕ5  \u_к555ие5_2  (
    .C2__14(T9), .C1__1(T10), .R0__2(nand_4_out), .R0__3(T16), ._1__12(T10), ._2__9(T11), ._4__8(T12),
    ._8__11(T13));
  \К555ИЕ5  \u_к555ие5_3  (
    .C2__14(T13), .C1__1(T14), .R0__2(nand_4_out), .R0__3(T16), ._1__12(T14), ._2__9(T16),
    ._4__8(\к555ие5_3__4__8 ), ._8__11(\к555ие5_3__8__11 ));
  not not_1 (not_1_out, T9);
  and and_1 (and_1_out, START, clock_1_out);
  not not_2 (not_2_out, and_1_out);
  nor nor_1 (nor_1_out, T5, T6);
  nand nand_1 (nand_1_out, T7, T8);
  nand nand_2 (nand_2_out, T10, T12);
  nand nand_3 (nand_3_out, T10, T11, T12);
  nor nor_2 (nor_2_out, T16, nor_1_out);
  not not_3 (not_3_out, nor_1_out);
  nand nand_4 (nand_4_out, nand_3_out, nand_3_out, nand_3_out);
  \К555ИЕ7  \u_к555ие7_2  (
    .D1__15(1'b1), .minus_1__4(1'b1), .plus_1__5(not_2_out), .D2__1(1'b1), .D4__10(1'b1), .D8__9(1'b1),
    .R__14(RESET), .V__11(1'b1), .P___13(\к555ие7_2_p___13 ), .P___12(\к555ие7_2_p___12 ),
    ._1__3(\к555ие7_2__1__3 ), ._2__2(T15), ._4__6(\к555ие7_2__4__6 ), ._8__7(T1));
  nor nor_3 (nor_3_out, nor_2_out, nor_2_out);
  nor nor_4 (nor_4_out, not_3_out, T4);
  nand nand_5 (A_VD2, T11, T11, T10, nand_1_out, not_1_out, nand_2_out, T16, T16);
  nand nand_6 (A_VD3, nor_4_out, T3);
  \К555ИД4  \u_к555ид4_1  (
    .\С1__1 (\к555ие7_2__4__6 ), .nD1__2(nor_3_out), .A0__13(\к555ие7_2__1__3 ), .A1__3(T15), .nD2__15(1'b0),
    .nC2__14(1'b0), .nA0__7(\к555ид4_1_na0__7 ), .nA1__6(\к555ид4_1_na1__6 ), .nA2__5(\к555ид4_1_na2__5 ),
    .nA3__4(\к555ид4_1_na3__4 ), .nB0__9(\к555ид4_1_nb0__9 ), .nB1__10(T17), .nB2__11(\к555ид4_1_nb2__11 ),
    .nB3__12(T18));
  not not_4 (C1_C2_RG, not_2_out);
  not not_5 (V_RG, \к555ид4_1_na3__4 );
  nand nand_7 (RAS_RAM_CS1_R6_A_MX, \к555ид4_1_nb0__9 , T18);
  nand nand_8 (\Ф2_CPU , \к555ид4_1_nb0__9 , \к555ид4_1_nb2__11 );
  nand nand_9 (\Ф1_CPU , T18, T18);
endmodule

module \RS_триггер_синхронный  (
  input  S,
  input  C,
  input  R,
  output Q,
  output nQ
);

  wire nand_1_out, nand_2_out;

  nand nand_1 (nand_1_out, S, C);
  nand nand_2 (nand_2_out, C, R);
  nand nand_3 (Q, nand_1_out, nQ);
  nand nand_4 (nQ, Q, nand_2_out);
endmodule

module \К555TM2  (
  input  Set__nSD,
  input  Clock,
  input  D,
  input  Clear__nCD,
  output Q,
  output nQ
);

  wire nand_1_out, nand_2_out, nand_3_out, nand_4_out, not_1_out, not_2_out;

  not not_1 (not_1_out, Set__nSD);
  not not_2 (not_2_out, Clear__nCD);
  nand nand_1 (nand_1_out, not_1_out, nand_4_out, nand_2_out);
  nand nand_2 (nand_2_out, nand_1_out, not_2_out, Clock);
  nand nand_3 (nand_3_out, nand_2_out, Clock, nand_4_out);
  nand nand_4 (nand_4_out, nand_3_out, not_2_out, D);
  nand nand_5 (Q, not_1_out, nand_2_out, nQ);
  nand nand_6 (nQ, Q, not_2_out, nand_3_out);
endmodule

module \К555ИЕ7  (
  input  D1__15,
  input  minus_1__4,
  input  plus_1__5,
  input  D2__1,
  input  D4__10,
  input  D8__9,
  input  R__14,
  input  V__11,
  output P___13,
  output P___12,
  output _1__3,
  output _2__2,
  output _4__6,
  output _8__7
);

  wire and_1_out, and_2_out, and_3_out, and_4_out, and_5_out, and_6_out, nand_1_out, nand_2_out, nand_3_out,
       nand_4_out, nand_7_out, nand_8_out, nand_9_out, nand_10_out, not_1_out, not_2_out, not_3_out,
       not_4_out, not_5_out, not_6_out, not_7_out, not_8_out, not_9_out, not_10_out, not_11_out, not_12_out,
       or_1_out, or_2_out, or_3_out, or_4_out, or_5_out, or_6_out, or_7_out, or_8_out, \к555tm2_1_nq ,
       \к555tm2_2_nq , \к555tm2_3_nq , \к555tm2_4_nq ;

  not not_1 (not_1_out, minus_1__4);
  not not_2 (not_2_out, plus_1__5);
  not not_3 (not_3_out, R__14);
  not not_4 (not_4_out, V__11);
  nand nand_1 (nand_1_out, D1__15, not_4_out, not_3_out);
  nand nand_2 (nand_2_out, D2__1, not_4_out, not_3_out);
  and and_1 (and_1_out, not_1_out, \к555tm2_1_nq );
  and and_2 (and_2_out, _1__3, not_2_out);
  nand nand_3 (nand_3_out, D4__10, not_4_out, not_3_out);
  and and_3 (and_3_out, not_1_out, \к555tm2_1_nq , \к555tm2_2_nq );
  and and_4 (and_4_out, _1__3, _2__2, not_2_out);
  nand nand_4 (nand_4_out, D8__9, not_4_out, not_3_out);
  and and_5 (and_5_out, not_1_out, \к555tm2_1_nq , \к555tm2_2_nq , \к555tm2_3_nq );
  and and_6 (and_6_out, _1__3, _2__2, _4__6, not_2_out);
  or or_1 (or_1_out, not_1_out, not_2_out);
  or or_2 (or_2_out, and_1_out, and_2_out);
  or or_3 (or_3_out, and_3_out, and_4_out);
  or or_4 (or_4_out, and_5_out, and_6_out);
  nand nand_5 (P___13, not_1_out, \к555tm2_1_nq , \к555tm2_2_nq , \к555tm2_3_nq , \к555tm2_4_nq );
  nand nand_6 (P___12, _1__3, _2__2, _4__6, _8__7, not_2_out);
  nand nand_7 (nand_7_out, nand_1_out, not_4_out);
  nand nand_8 (nand_8_out, nand_2_out, not_4_out);
  nand nand_9 (nand_9_out, nand_3_out, not_4_out);
  nand nand_10 (nand_10_out, nand_4_out, not_4_out);
  not not_5 (not_5_out, or_1_out);
  not not_6 (not_6_out, or_2_out);
  not not_7 (not_7_out, or_3_out);
  not not_8 (not_8_out, or_4_out);
  not not_9 (not_9_out, nand_1_out);
  \К555TM2  \u_к555tm2_1  (
    .Set__nSD(not_9_out), .Clear__nCD(or_5_out), .Clock(not_5_out), .Q(_1__3), .nQ(\к555tm2_1_nq ),
    .D(\к555tm2_1_nq ));
  or or_5 (or_5_out, ~not_3_out, ~nand_7_out);  // OR_Gate
  not not_10 (not_10_out, nand_2_out);
  \К555TM2  \u_к555tm2_2  (
    .Set__nSD(not_10_out), .Clear__nCD(or_6_out), .Clock(not_6_out), .Q(_2__2), .nQ(\к555tm2_2_nq ),
    .D(\к555tm2_2_nq ));
  or or_6 (or_6_out, ~not_3_out, ~nand_8_out);  // OR_Gate
  not not_11 (not_11_out, nand_3_out);
  \К555TM2  \u_к555tm2_3  (
    .Set__nSD(not_11_out), .Clear__nCD(or_7_out), .Clock(not_7_out), .Q(_4__6), .nQ(\к555tm2_3_nq ),
    .D(\к555tm2_3_nq ));
  or or_7 (or_7_out, ~not_3_out, ~nand_9_out);  // OR_Gate
  not not_12 (not_12_out, nand_4_out);
  \К555TM2  \u_к555tm2_4  (
    .Set__nSD(not_12_out), .Clear__nCD(or_8_out), .Clock(not_8_out), .Q(_8__7), .nQ(\к555tm2_4_nq ),
    .D(\к555tm2_4_nq ));
  or or_8 (or_8_out, ~not_3_out, ~nand_10_out);  // OR_Gate
endmodule

module \JK_триггер_синхронный  (
  input  J,
  input  C,
  input  K,
  output Q,
  output nQ
);

  wire and_1_out, and_2_out;

  and and_1 (and_1_out, C, K);
  and and_2 (and_2_out, J, C);
  nor nor_1 (K, and_2_out, J);
  nor nor_2 (J, K, and_1_out);

  assign nQ = J;
  assign Q = K;
endmodule

module \К555ИД4  (
  input  nD1__2,
  input  \С1__1 ,
  input  A0__13,
  input  A1__3,
  input  nD2__15,
  input  nC2__14,
  output nA0__7,
  output nA1__6,
  output nA2__5,
  output nA3__4,
  output nB0__9,
  output nB1__10,
  output nB2__11,
  output nB3__12
);

  wire and_1_out, and_2_out, not_1_out, not_2_out, not_3_out, not_4_out;

  and and_1 (and_1_out, ~nD1__2, \С1__1 );  // AND_Gate
  not not_1 (not_1_out, A0__13);
  not not_2 (not_2_out, A1__3);
  and and_2 (and_2_out, ~nD2__15, ~nC2__14);  // AND_Gate
  not not_3 (not_3_out, not_1_out);
  not not_4 (not_4_out, not_2_out);
  nand nand_1 (nA0__7, not_1_out, not_2_out, and_1_out);
  nand nand_2 (nA1__6, and_1_out, not_2_out, not_3_out);
  nand nand_3 (nA2__5, and_1_out, not_1_out, not_4_out);
  nand nand_4 (nA3__4, and_1_out, not_3_out, not_4_out);
  nand nand_5 (nB0__9, not_1_out, not_2_out, and_2_out);
  nand nand_6 (nB1__10, and_2_out, not_2_out, not_3_out);
  nand nand_7 (nB2__11, and_2_out, not_1_out, not_4_out);
  nand nand_8 (nB3__12, and_2_out, not_3_out, not_4_out);
endmodule

module \К555ТВ9_JK_триггер_с_установкой_и_сбросом  (
  input  SET__nSD,
  input  J,
  input  CLOCK__CP,
  input  \К ,
  input  CLEAR__nCD,
  output Q,
  output nQ
);

  wire and_1_out, and_2_out, and_3_out, and_4_out, nand_1_out, nand_2_out;

  nor nor_1 (Q, and_1_out, and_2_out);
  and and_1 (and_1_out, nQ, nand_1_out, SET__nSD);
  and and_2 (and_2_out, SET__nSD, CLOCK__CP, nQ);
  nand nand_1 (nand_1_out, nQ, CLEAR__nCD, J, CLOCK__CP);
  nand nand_2 (nand_2_out, Q, SET__nSD, \К , CLOCK__CP);
  and and_3 (and_3_out, Q, nand_2_out, CLEAR__nCD);
  and and_4 (and_4_out, CLEAR__nCD, CLOCK__CP, Q);
  nor nor_2 (nQ, and_3_out, and_4_out);
endmodule

module \Временный_JK_триггер_с_установкой_и_сбросом  (
  input  SET__nSD,
  input  J,
  input  CLOCK__CP,
  input  \К ,
  input  CLEAR__nCD,
  output Q,
  output nQ
);

  wire and_1_out, j_k_ff_1_q, j_k_ff_1_qn, not_1_out, not_2_out, not_3_out;

  not not_1 (not_1_out, CLOCK__CP);
  not not_2 (not_2_out, CLEAR__nCD);
  J_K_Flip_Flop j_k_ff_1 (
    .J(J), .clk(not_1_out), .K(\К ), .Q(j_k_ff_1_q), .Qn(j_k_ff_1_qn), .preset(not_3_out), .reset(not_2_out));  // open: en
  not not_3 (not_3_out, SET__nSD);
  and and_1 (and_1_out, not_3_out, not_2_out);
  or or_1 (Q, j_k_ff_1_q, and_1_out);
  or or_2 (nQ, j_k_ff_1_qn, and_1_out);
endmodule

module \К555ИЕ5  (
  input  C2__14,
  input  C1__1,
  input  R0__2,
  input  R0__3,
  output _1__12,
  output _2__9,
  output _4__8,
  output _8__11
);

  wire nand_1_out;

  nand nand_1 (nand_1_out, R0__2, R0__3);
  \Временный_JK_триггер_с_установкой_и_сбросом  \u_временный_jk_триггер_с_установкой_и_сбросом_1  (
    .J(1'b1), .CLOCK__CP(C2__14), .\К (1'b1), .Q(_1__12), .SET__nSD(1'b1), .CLEAR__nCD(nand_1_out));  // open: nQ
  \Временный_JK_триггер_с_установкой_и_сбросом  \u_временный_jk_триггер_с_установкой_и_сбросом_2  (
    .J(1'b1), .CLOCK__CP(C1__1), .\К (1'b1), .Q(_2__9), .SET__nSD(1'b1), .CLEAR__nCD(nand_1_out));  // open: nQ
  \Временный_JK_триггер_с_установкой_и_сбросом  \u_временный_jk_триггер_с_установкой_и_сбросом_3  (
    .J(1'b1), .CLOCK__CP(_2__9), .\К (1'b1), .Q(_4__8), .SET__nSD(1'b1), .CLEAR__nCD(nand_1_out));  // open: nQ
  \Временный_JK_триггер_с_установкой_и_сбросом  \u_временный_jk_триггер_с_установкой_и_сбросом_4  (
    .J(1'b1), .CLOCK__CP(_4__8), .\К (1'b1), .Q(_8__11), .SET__nSD(1'b1), .CLEAR__nCD(nand_1_out));  // open: nQ
endmodule
